// Logisim project oblig1.circ as structural Verilog: 4 circuits, main circuit main
module main (
  input  A3,
  input  A2,
  input  A1,
  input  A0,
  output S7,
  output S6,
  output S5,
  output S4,
  output S3,
  output S2,
  output S1,
  output S0
);

  wire A1_A3_C0_c1, A2_A1_c0, A2_C1_c3;

  A_C A3_C2 (.C3(S7), .A2(A3), .S5(S6), .C2(A2_C1_c3));
  A_C A2_C1 (.C3(A2_C1_c3), .A2(A2), .S5(S5), .C2(A1_A3_C0_c1));
  Fulladder A1_A3_C0 (.C1(A1_A3_C0_c1), .A3(A3), .A1(A1), .S4(S4), .C0(A2_A1_c0));
  A0_A2 A2_A1 (.C0(A2_A1_c0), .A2(A2), .A1(A0), .S3(S3));

  assign S0 = 1'b0;
  assign S1 = A0;
  assign S2 = A1;
endmodule

module A0_A2 (
  input  A2,
  input  A1,
  output S3,
  output C0
);

  and and_1 (C0, A2, A1);
  xor xor_1 (S3, A2, A1);
endmodule

module Fulladder (
  input  C0,
  input  A3,
  input  A1,
  output C1,
  output S4
);

  wire A1_A3_out, A1XORA3_out, C4_A1XorA3_out;

  or or_1 (C1, A1_A3_out, C4_A1XorA3_out);
  and A1_A3 (A1_A3_out, A1, A3);
  xor A1XORA3 (A1XORA3_out, A3, A1);
  and C4_A1XorA3 (C4_A1XorA3_out, A1XORA3_out, C0);
  xor A1xorA3xorC4 (S4, A1XORA3_out, C0);
endmodule

module A_C (
  input  A2,
  input  C2,
  output S5,
  output C3
);

  and and_1 (C3, A2, C2);
  xor xor_1 (S5, A2, C2);
endmodule
